// Digital circuit 0~7_7~0.dig as structural Verilog
module _0_7_7_0 (
  input  clk,
  input  x,
  input  in_3
);

  wire and_1_out, and_2_out, and_3_out, and_4_out, and_5_out, and_6_out, and_7_out, and_8_out, and_9_out,
       and_10_out, jk_ff_1_q, jk_ff_2_nq, jk_ff_2_q, jk_ff_3_nq, jk_ff_3_q, not_1_out, not_2_out, or_1_out,
       or_2_out, or_3_out, or_4_out;

  not not_1 (not_1_out, x);
  not not_2 (not_2_out, not_1_out);
  and and_1 (and_1_out, and_9_out, not_1_out);
  and and_2 (and_2_out, and_10_out, not_2_out);
  and and_3 (and_3_out, and_9_out, not_1_out);
  and and_4 (and_4_out, and_10_out, not_2_out);
  and and_5 (and_5_out, jk_ff_3_q, not_1_out);
  and and_6 (and_6_out, jk_ff_3_nq, not_2_out);
  and and_7 (and_7_out, jk_ff_3_q, not_1_out);
  and and_8 (and_8_out, jk_ff_3_nq, not_2_out);
  or or_1 (or_1_out, and_1_out, and_2_out);
  or or_2 (or_2_out, and_3_out, and_4_out);
  or or_3 (or_3_out, and_5_out, and_6_out);
  or or_4 (or_4_out, and_7_out, and_8_out);
  JK_FF jk_ff_1 (.J(or_1_out), .C(clk), .K(or_2_out), .Q(jk_ff_1_q));  // open: nQ
  JK_FF jk_ff_2 (.J(or_3_out), .C(clk), .K(or_4_out), .Q(jk_ff_2_q), .nQ(jk_ff_2_nq));
  JK_FF jk_ff_3 (.J(in_3), .C(clk), .K(in_3), .Q(jk_ff_3_q), .nQ(jk_ff_3_nq));
  and and_9 (and_9_out, jk_ff_2_q, jk_ff_3_q);
  and and_10 (and_10_out, jk_ff_2_nq, jk_ff_3_nq);
  LED _4 (.in(jk_ff_1_q));
  LED _2 (.in(jk_ff_2_q));
  LED _1 (.in(jk_ff_3_q));

  // Notes on the sheet:
  //   in_3: default 1
endmodule
