// Digital circuit 除法實作.dig as structural Verilog
module \除法實作  (
  input  e_2,
  input  f_2,
  input  g_2,
  input  dp,
  input  d_2,
  input  c_2,
  input  b_2,
  input  a_2,
  input  dp_2,
  input  _0,
  input  _1,
  input  _2,
  input  _3,
  input  _4,
  input  _5,
  input  _6,
  input  _7,
  input  _8,
  input  _9,
  input  dp_3,
  input  _20,
  input  _21,
  input  _22,
  input  _23,
  input  _24,
  input  _25,
  input  _26,
  input  _27,
  input  _28,
  input  _29,
  input  dp_4,
  input  _30,
  input  _31,
  input  _32,
  input  _33,
  input  _34,
  input  _35,
  input  _36,
  input  _37,
  input  _38,
  input  _39,
  input  dp_5,
  input  _50,
  input  _51,
  input  _52,
  input  _53,
  input  _54,
  input  _55,
  input  _56,
  input  _57,
  input  _58,
  input  _59,
  input  dp_6,
  input  _60,
  input  _61,
  input  _62,
  input  _63,
  input  _64,
  input  _65,
  input  _66,
  input  _67,
  input  _68,
  input  _69,
  output a,
  output b,
  output c,
  output d,
  output e,
  output f,
  output g,
  output a_3,
  output b_3,
  output c_3,
  output d_3,
  output e_3,
  output f_3,
  output g_3,
  output a_4,
  output b_4,
  output c_4,
  output d_4,
  output e_4,
  output f_4,
  output g_4,
  output a_5,
  output b_5,
  output c_5,
  output d_5,
  output e_5,
  output f_5,
  output g_5,
  output a_6,
  output b_6,
  output c_6,
  output d_6,
  output e_6,
  output f_6,
  output g_6
);

  wire and_1_out, and_2_out, and_3_out, and_4_out, and_5_out, and_6_out, and_7_out, and_8_out, and_9_out,
       and_10_out, and_11_out, and_12_out, and_13_out, and_14_out, and_15_out, and_16_out, and_17_out,
       and_18_out, and_19_out, and_20_out, and_21_out, and_22_out, and_23_out, and_24_out, and_25_out,
       and_26_out, and_27_out, and_28_out, and_29_out, and_30_out, and_31_out, and_32_out, and_33_out,
       and_34_out, and_35_out, and_36_out, and_37_out, and_38_out, and_39_out, and_40_out, and_41_out,
       and_42_out, and_43_out, and_44_out, and_45_out, and_46_out, and_47_out, and_48_out, and_49_out,
       and_50_out, and_51_out, and_52_out, and_53_out, and_54_out, and_55_out, and_56_out, and_57_out,
       and_58_out, and_59_out, and_60_out, and_61_out, and_62_out, and_63_out, and_64_out, and_65_out,
       and_66_out, and_67_out, and_68_out, and_69_out, and_70_out, and_71_out, and_72_out, and_73_out,
       and_74_out, and_75_out, and_76_out, and_77_out, and_78_out, and_79_out, and_80_out, not_1_out,
       not_2_out, not_3_out, not_4_out, not_5_out, not_6_out, not_7_out, not_8_out, not_9_out, not_10_out,
       not_11_out, not_12_out, not_13_out, not_14_out, not_15_out, or_1_out, or_2_out, or_3_out, or_5_out,
       or_12_out, or_13_out, or_14_out, or_16_out, or_23_out, or_24_out, or_25_out, or_27_out, or_34_out,
       or_35_out, or_36_out, or_37_out, or_39_out, or_40_out, or_43_out, or_49_out;

  or or_1 (or_1_out, _58, _59);
  not not_1 (not_1_out, or_2_out);
  or or_2 (or_2_out, _54, _55, _56, _57);
  not not_2 (not_2_out, or_3_out);
  or or_3 (or_3_out, _52, _53, _56, _57);
  not not_3 (not_3_out, or_5_out);
  and and_1 (and_1_out, or_2_out, or_5_out);
  and and_2 (and_2_out, not_1_out, not_3_out);
  and and_3 (and_3_out, not_2_out, not_3_out);
  and and_4 (and_4_out, or_3_out, or_5_out);
  or or_4 (c_5, or_2_out, not_2_out, or_5_out);
  and and_5 (and_5_out, not_1_out, not_3_out);
  and and_6 (and_6_out, or_2_out, not_2_out, or_5_out);
  and and_7 (and_7_out, not_1_out, or_3_out);
  and and_8 (and_8_out, or_3_out, not_3_out);
  and and_9 (and_9_out, not_1_out, not_3_out);
  and and_10 (and_10_out, or_3_out, not_3_out);
  and and_11 (and_11_out, or_2_out, not_2_out);
  and and_12 (and_12_out, or_2_out, not_3_out);
  and and_13 (and_13_out, not_2_out, not_3_out);
  and and_14 (and_14_out, or_2_out, not_2_out);
  and and_15 (and_15_out, not_1_out, or_3_out);
  and and_16 (and_16_out, or_3_out, not_3_out);
  or or_5 (or_5_out, _51, _53, _55, _57, _59);
  or or_6 (a_5, or_1_out, and_1_out, and_2_out, or_3_out);
  or or_7 (b_5, not_1_out, and_3_out, and_4_out);
  or or_8 (d_5, or_1_out, and_5_out, and_6_out, and_7_out, and_8_out);
  or or_9 (e_5, and_9_out, and_10_out);
  or or_10 (f_5, or_1_out, and_11_out, and_12_out, and_13_out);
  or or_11 (g_5, or_1_out, and_14_out, and_15_out, and_16_out);
  Seven_Seg seven_seg_1 (.a(a_5), .b(b_5), .c(c_5), .d(d_5), .e(e_5), .f(f_5), .g(g_5), .dp(dp_5));
  or or_12 (or_12_out, _38, _39);
  not not_4 (not_4_out, or_13_out);
  or or_13 (or_13_out, _34, _35, _36, _37);
  not not_5 (not_5_out, or_14_out);
  or or_14 (or_14_out, _32, _33, _36, _37);
  not not_6 (not_6_out, or_16_out);
  and and_17 (and_17_out, or_13_out, or_16_out);
  and and_18 (and_18_out, not_4_out, not_6_out);
  and and_19 (and_19_out, not_5_out, not_6_out);
  and and_20 (and_20_out, or_14_out, or_16_out);
  or or_15 (c_4, or_13_out, not_5_out, or_16_out);
  and and_21 (and_21_out, not_4_out, not_6_out);
  and and_22 (and_22_out, or_13_out, not_5_out, or_16_out);
  and and_23 (and_23_out, not_4_out, or_14_out);
  and and_24 (and_24_out, or_14_out, not_6_out);
  and and_25 (and_25_out, not_4_out, not_6_out);
  and and_26 (and_26_out, or_14_out, not_6_out);
  and and_27 (and_27_out, or_13_out, not_5_out);
  and and_28 (and_28_out, or_13_out, not_6_out);
  and and_29 (and_29_out, not_5_out, not_6_out);
  and and_30 (and_30_out, or_13_out, not_5_out);
  and and_31 (and_31_out, not_4_out, or_14_out);
  and and_32 (and_32_out, or_14_out, not_6_out);
  or or_16 (or_16_out, _31, _33, _35, _37, _39);
  or or_17 (a_4, or_12_out, and_17_out, and_18_out, or_14_out);
  or or_18 (b_4, not_4_out, and_19_out, and_20_out);
  or or_19 (d_4, or_12_out, and_21_out, and_22_out, and_23_out, and_24_out);
  or or_20 (e_4, and_25_out, and_26_out);
  or or_21 (f_4, or_12_out, and_27_out, and_28_out, and_29_out);
  or or_22 (g_4, or_12_out, and_30_out, and_31_out, and_32_out);
  Seven_Seg seven_seg_2 (.a(a_4), .b(b_4), .c(c_4), .d(d_4), .e(e_4), .f(f_4), .g(g_4), .dp(dp_4));
  or or_23 (or_23_out, _28, _29);
  or or_24 (or_24_out, _24, _25, _26, _27);
  not not_7 (not_7_out, or_24_out);
  not not_8 (not_8_out, or_25_out);
  or or_25 (or_25_out, _22, _23, _26, _27);
  not not_9 (not_9_out, or_27_out);
  and and_33 (and_33_out, or_24_out, or_27_out);
  and and_34 (and_34_out, not_7_out, not_9_out);
  and and_35 (and_35_out, not_8_out, not_9_out);
  and and_36 (and_36_out, or_25_out, or_27_out);
  or or_26 (c_3, or_24_out, not_8_out, or_27_out);
  and and_37 (and_37_out, not_7_out, not_9_out);
  and and_38 (and_38_out, or_24_out, not_8_out, or_27_out);
  and and_39 (and_39_out, not_7_out, or_25_out);
  and and_40 (and_40_out, or_25_out, not_9_out);
  and and_41 (and_41_out, not_7_out, not_9_out);
  and and_42 (and_42_out, or_25_out, not_9_out);
  and and_43 (and_43_out, or_24_out, not_8_out);
  and and_44 (and_44_out, or_24_out, not_9_out);
  and and_45 (and_45_out, not_8_out, not_9_out);
  and and_46 (and_46_out, or_24_out, not_8_out);
  and and_47 (and_47_out, not_7_out, or_25_out);
  and and_48 (and_48_out, or_25_out, not_9_out);
  or or_27 (or_27_out, _21, _23, _25, _27, _29);
  or or_28 (a_3, or_23_out, and_33_out, and_34_out, or_25_out);
  or or_29 (b_3, not_7_out, and_35_out, and_36_out);
  or or_30 (d_3, or_23_out, and_37_out, and_38_out, and_39_out, and_40_out);
  or or_31 (e_3, and_41_out, and_42_out);
  or or_32 (f_3, or_23_out, and_43_out, and_44_out, and_45_out);
  or or_33 (g_3, or_23_out, and_46_out, and_47_out, and_48_out);
  Seven_Seg seven_seg_3 (.a(a_3), .b(b_3), .c(c_3), .d(d_3), .e(e_3), .f(f_3), .g(g_3), .dp(dp_3));
  or or_34 (or_34_out, _8, _9);
  or or_35 (or_35_out, _4, _5, _6, _7);
  not not_10 (not_10_out, or_35_out);
  or or_36 (or_36_out, _68, _69);
  not not_11 (not_11_out, or_37_out);
  not not_12 (not_12_out, or_40_out);
  not not_13 (not_13_out, or_39_out);
  or or_37 (or_37_out, _2, _3, _6, _7);
  and and_49 (and_49_out, or_35_out, or_40_out);
  and and_50 (and_50_out, not_10_out, not_12_out);
  and and_51 (and_51_out, not_11_out, not_12_out);
  and and_52 (and_52_out, or_37_out, or_40_out);
  or or_38 (c, or_35_out, not_11_out, or_40_out);
  and and_53 (and_53_out, not_10_out, not_12_out);
  and and_54 (and_54_out, or_35_out, not_11_out, or_40_out);
  and and_55 (and_55_out, not_10_out, or_37_out);
  and and_56 (and_56_out, or_37_out, not_12_out);
  and and_57 (and_57_out, not_10_out, not_12_out);
  and and_58 (and_58_out, or_37_out, not_12_out);
  and and_59 (and_59_out, or_35_out, not_11_out);
  and and_60 (and_60_out, or_35_out, not_12_out);
  and and_61 (and_61_out, not_11_out, not_12_out);
  and and_62 (and_62_out, or_35_out, not_11_out);
  and and_63 (and_63_out, not_10_out, or_37_out);
  and and_64 (and_64_out, or_37_out, not_12_out);
  or or_39 (or_39_out, _64, _65, _66, _67);
  not not_14 (not_14_out, or_43_out);
  or or_40 (or_40_out, _1, _3, _5, _7, _9);
  or or_41 (b, not_10_out, and_51_out, and_52_out);
  or or_42 (e, and_57_out, and_58_out);
  or or_43 (or_43_out, _62, _63, _66, _67);
  not not_15 (not_15_out, or_49_out);
  and and_65 (and_65_out, or_39_out, or_49_out);
  and and_66 (and_66_out, not_13_out, not_15_out);
  and and_67 (and_67_out, not_14_out, not_15_out);
  and and_68 (and_68_out, or_43_out, or_49_out);
  or or_44 (c_6, or_39_out, not_14_out, or_49_out);
  and and_69 (and_69_out, not_13_out, not_15_out);
  and and_70 (and_70_out, or_39_out, not_14_out, or_49_out);
  and and_71 (and_71_out, not_13_out, or_43_out);
  and and_72 (and_72_out, or_43_out, not_15_out);
  and and_73 (and_73_out, not_13_out, not_15_out);
  and and_74 (and_74_out, or_43_out, not_15_out);
  and and_75 (and_75_out, or_39_out, not_14_out);
  and and_76 (and_76_out, or_39_out, not_15_out);
  and and_77 (and_77_out, not_14_out, not_15_out);
  and and_78 (and_78_out, or_39_out, not_14_out);
  and and_79 (and_79_out, not_13_out, or_43_out);
  and and_80 (and_80_out, or_43_out, not_15_out);
  or or_45 (a, or_34_out, and_49_out, and_50_out, or_37_out);
  or or_46 (d, or_34_out, and_53_out, and_54_out, and_55_out, and_56_out);
  or or_47 (f, or_34_out, and_59_out, and_60_out, and_61_out);
  or or_48 (g, or_34_out, and_62_out, and_63_out, and_64_out);
  or or_49 (or_49_out, _61, _63, _65, _67, _69);
  or or_50 (a_6, or_36_out, and_65_out, and_66_out, or_43_out);
  or or_51 (b_6, not_13_out, and_67_out, and_68_out);
  or or_52 (d_6, or_36_out, and_69_out, and_70_out, and_71_out, and_72_out);
  or or_53 (e_6, and_73_out, and_74_out);
  or or_54 (f_6, or_36_out, and_75_out, and_76_out, and_77_out);
  or or_55 (g_6, or_36_out, and_78_out, and_79_out, and_80_out);
  Seven_Seg seven_seg_4 (.a(a), .b(b), .c(c), .d(d), .e(e), .f(f), .g(g), .dp(dp_2));
  Seven_Seg seven_seg_5 (.a(a_6), .b(b_6), .c(c_6), .d(d_6), .e(e_6), .f(f_6), .g(g_6), .dp(dp_6));
  Seven_Seg seven_seg_6 (.a(a_2), .b(b_2), .c(c_2), .d(d_2), .e(e_2), .f(f_2), .g(g_2), .dp(dp));
endmodule
